// Logisim project Projeto.circ as structural Verilog: 7 circuits, main circuit main
module main (
  input  [1:0] xy,
  input  [3:0] B,
  input  [3:0] A,
  output [3:0] S,
  output [3:0] S_2,
  output [3:0] S_3,
  output [3:0] S_4,
  output Overflow,
  output Overflow_2
);

  Add_4 add_4_1 (.A(A), .Overflow(Overflow), .S(S_2), .B(B));
  Sub_4 sub_4_1 (.A(A), .Overflow(Overflow_2), .S(S_3), .B(B));
  Rot_Esq rot_esq_1 (.abcd(A), .xy(xy), .ABCD_2(S));
  Rot_Dir rot_dir_1 (.abcd(A), .xy(xy), .ABCD_2(S_4));
endmodule

module Add_1 (
  input  A,
  input  B,
  input  C,
  output S,
  output Vai_1
);

  wire and_1_out, and_2_out, or_1_out, xor_1_out;

  xor xor_1 (xor_1_out, C, B);
  xor xor_2 (S, xor_1_out, A);
  or or_1 (or_1_out, C, B);
  and and_1 (and_1_out, or_1_out, A);
  and and_2 (and_2_out, C, B);
  or or_2 (Vai_1, and_1_out, and_2_out);
endmodule

module Add_4 (
  input  [3:0] B,
  input  [3:0] A,
  output Overflow,
  output [3:0] S
);

  wire add_1_2_vai_1, add_1_3_vai_1, add_1_4_vai_1;

  Add_1 add_1_1 (.S(S[3]), .Vai_1(Overflow), .A(A[3]), .B(B[3]), .C(add_1_2_vai_1));
  Add_1 add_1_2 (.S(S[2]), .Vai_1(add_1_2_vai_1), .A(A[2]), .B(B[2]), .C(add_1_3_vai_1));
  Add_1 add_1_3 (.S(S[1]), .Vai_1(add_1_3_vai_1), .A(A[1]), .B(B[1]), .C(add_1_4_vai_1));
  Add_1 add_1_4 (.S(S[0]), .Vai_1(add_1_4_vai_1), .A(A[0]), .B(B[0]), .C(1'b0));
endmodule

module Sub_1 (
  input  A,
  input  B,
  input  C,
  output S,
  output Vai_1
);

  wire and_1_out, and_2_out, or_1_out, xor_1_out;

  xor xor_1 (xor_1_out, C, B);
  or or_1 (or_1_out, C, B);
  and and_1 (and_1_out, or_1_out, ~A);  // AND_Gate
  and and_2 (and_2_out, C, B);
  xor xor_2 (S, xor_1_out, A);
  or or_2 (Vai_1, and_1_out, and_2_out);
endmodule

module Sub_4 (
  input  [3:0] B,
  input  [3:0] A,
  output Overflow,
  output [3:0] S
);

  wire sub_1_1_vai_1, sub_1_3_vai_1, sub_1_4_vai_1;

  // Probe on A
  Sub_1 sub_1_1 (.S(S[2]), .Vai_1(sub_1_1_vai_1), .A(A[2]), .B(B[2]), .C(sub_1_3_vai_1));
  Sub_1 sub_1_2 (.S(S[3]), .Vai_1(Overflow), .A(A[3]), .B(B[3]), .C(sub_1_1_vai_1));
  // Probe on S
  Sub_1 sub_1_3 (.S(S[1]), .Vai_1(sub_1_3_vai_1), .A(A[1]), .B(B[1]), .C(sub_1_4_vai_1));
  Sub_1 sub_1_4 (.S(S[0]), .Vai_1(sub_1_4_vai_1), .A(A[0]), .B(B[0]), .C(1'b0));
  // Probe on B
endmodule

module Rot_Esq (
  input  [3:0] abcd,
  input  [1:0] xy,
  output [3:0] ABCD_2
);

  wire and_1_out, and_2_out, and_3_out, and_4_out, and_5_out, and_6_out, and_7_out, and_8_out, and_9_out;

  and and_1 (and_1_out, ~xy[1], ~xy[0], abcd[3]);  // AND_Gate
  and and_2 (and_2_out, ~xy[1], xy[0], abcd[2]);  // AND_Gate
  and and_3 (and_3_out, xy[1], ~xy[0], abcd[1]);  // AND_Gate
  and and_4 (and_4_out, xy[1], xy[0], abcd[0]);
  and and_5 (and_5_out, ~xy[1], ~xy[0], abcd[2]);  // AND_Gate
  and and_6 (and_6_out, ~xy[1], xy[0], abcd[1]);  // AND_Gate
  and and_7 (and_7_out, xy[1], ~xy[0], abcd[0]);  // AND_Gate
  and and_8 (and_8_out, ~xy[1], ~xy[0], abcd[1]);  // AND_Gate
  and and_9 (and_9_out, ~xy[1], xy[0], abcd[0]);  // AND_Gate
  and and_10 (ABCD_2[0], ~xy[1], ~xy[0], abcd[0]);  // AND_Gate
  or or_1 (ABCD_2[3], and_1_out, and_2_out, and_3_out, and_4_out);
  or or_2 (ABCD_2[2], and_5_out, and_6_out, and_7_out);
  or or_3 (ABCD_2[1], and_8_out, and_9_out);
endmodule

module Rot_Dir (
  input  [3:0] abcd,
  input  [1:0] xy,
  output [3:0] ABCD_2
);

  wire and_1_out, and_2_out, and_3_out, and_4_out, and_5_out, and_6_out, and_7_out, and_8_out, and_9_out;

  and and_1 (and_1_out, ~xy[1], ~xy[0], abcd[0]);  // AND_Gate
  and and_2 (and_2_out, ~xy[1], xy[0], abcd[1]);  // AND_Gate
  and and_3 (and_3_out, xy[1], ~xy[0], abcd[2]);  // AND_Gate
  and and_4 (and_4_out, xy[1], xy[0], abcd[3]);
  and and_5 (and_5_out, ~xy[1], ~xy[0], abcd[1]);  // AND_Gate
  and and_6 (and_6_out, ~xy[1], xy[0], abcd[2]);  // AND_Gate
  and and_7 (and_7_out, xy[1], ~xy[0], abcd[3]);  // AND_Gate
  and and_8 (and_8_out, ~xy[1], ~xy[0], abcd[2]);  // AND_Gate
  and and_9 (and_9_out, ~xy[1], xy[0], abcd[3]);  // AND_Gate
  and and_10 (ABCD_2[3], ~xy[1], ~xy[0], abcd[3]);  // AND_Gate
  or or_1 (ABCD_2[0], and_1_out, and_2_out, and_3_out, and_4_out);
  or or_2 (ABCD_2[1], and_5_out, and_6_out, and_7_out);
  or or_3 (ABCD_2[2], and_8_out, and_9_out);

  // Notes on the sheet:
  //   Entradas
  //   Qtd. bits que desloca para a direita
endmodule
